# Fritzing sketch circuit_ (saved by Fritzing 0.9.3b)
breadboards: 1

parts:
  U1 = NodeMCU V1.0
  Part1 = US-100 Ultrasonic Rangefinder

nets:
  GND: U1.GND, Part1.GND
  N1: U1.D6, Part1.Echo/Rx
  N2: U1.D7, Part1.Trig/Tx
  VIN: U1.Vin, Part1.VCC

custom parts:
  NodeMCU V1.0: ESP8266 based NodeMCU
